// Logisim project 카운터 프로젝트.circ as structural Verilog: 1 circuit, main circuit main
module main (
  input  in_1
);

  wire clock_1_out, j_k_ff_1_q, j_k_ff_2_q, j_k_ff_3_q;

  Clock clock_1 (.out(clock_1_out));
  J_K_Flip_Flop j_k_ff_1 (.J(in_1), .clk(clock_1_out), .K(in_1), .Q(j_k_ff_1_q));  // open: Qn, preset, en, reset
  LED led_1 (.in(j_k_ff_1_q));
  J_K_Flip_Flop j_k_ff_2 (.J(in_1), .clk(j_k_ff_1_q), .K(in_1), .Q(j_k_ff_2_q));  // open: Qn, preset, en, reset
  LED led_2 (.in(j_k_ff_2_q));
  J_K_Flip_Flop j_k_ff_3 (.J(in_1), .clk(j_k_ff_2_q), .K(in_1), .Q(j_k_ff_3_q));  // open: Qn, preset, en, reset
  LED led_3 (.in(j_k_ff_3_q));
endmodule
